# Fritzing sketch skyping_wiring (saved by Fritzing 1.0.5)

parts:
  Mod1 = Amica NodeMCU DEVKIT 1.0
  A1 = DHT22 module
  TEMT6000_Breakout_Board1 = TEMT6000 Breakout Board [part_number=TEMT6000]

nets:
  N1: Mod1.pin1, Mod1.pin_26, A1.+, TEMT6000_Breakout_Board1.VCC
  N2: Mod1.pin2, Mod1.pin_25, Mod1.pin_29, A1.-, TEMT6000_Breakout_Board1.GND
  N3: Mod1.pin_14, A1.Out
  N4: Mod1.pin_16, TEMT6000_Breakout_Board1.SIG

custom parts:
  DHT22 module: DHT22 module. Pins VCC Data GND.
  TEMT6000 Breakout Board: The TEMT6000 is an ambient light sensor produced by Vishay Semiconductors. The sensor operates at both 3V3 and 5V and has analog output (with higher output voltage meaning more light) from the SIG pin.
