# Fritzing sketch skyping_wiring_firebeetle (saved by Fritzing 1.0.5)

parts:
  A1 = Solar power manger 5V
  M1 = FireBeetle ESP32-E
  TEMT6000_Breakout_Board1 = TEMT6000 Breakout Board [part_number=TEMT6000]
  A2 = DHT22 module
  U1 = LIPO-1000mAh [package=lipo-1000]  # not connected

nets:
  N1: A1.Pin_5, A1.Pin_7, A1.Pin_13, M1.pin_12, M1.pin_20, TEMT6000_Breakout_Board1.GND, A2.-
  N2: A1.Pin_8, A1.Pin_10, TEMT6000_Breakout_Board1.VCC, A2.+
  N3: A1.Pin_12, M1.pin_4
  N4: M1.pin_1, A2.Out
  N5: M1.pin_5, TEMT6000_Breakout_Board1.SIG

custom parts:
  Solar power manger 5V: Solar Power Manager 5V is a small power and high-efficiency solar power management module designed for 5V solar panel.
  FireBeetle ESP32-E: FireBeetle ESP32-E, specially designed for IoT, is an ESP-WROOM-32E-based main controller board with dual-core chips. It supports WiFi and Bluetooth dual-mode communication and features a small size, ultra-low power consumption, on-board charging circuit, and easy-to-use interface, which can be conveniently used for smart home IoT, industrial IoT applications, wearable devices, and so on. You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
  TEMT6000 Breakout Board: The TEMT6000 is an ambient light sensor produced by Vishay Semiconductors. The sensor operates at both 3V3 and 5V and has analog output (with higher output voltage meaning more light) from the SIG pin.
  DHT22 module: DHT22 module. Pins VCC Data GND.
